// Logisim project CPU2.circ as structural Verilog
module main (
  input  CLK,
  output SerialWrite,
  output [31:0] SerialOut,
  output [31:0] out_4
);

  wire AluA_EnableSigned, AluA_Left_UseConst, AluA_Right_UseConst, AluA_WriteOutput, and_1_out, and_3_out,
       and_4_out, and_7_out, big_rom_1_p1, big_rom_1_p2, big_rom_1_p3, button_1_out, CLK_t, comparator_1_eq,
       comparator_1_gt, comparator_1_lt, comparator_2_eq, comparator_2_gt, comparator_2_lt, comparator_3_gt,
       counter_3_carry, DivMod_SerialWriteASCII_Assembling, DivMod_SerialWriteASCII_Writing, DivMod_UseConst,
       DivMod_Write, DoJump, DoJump_IfCompare_AluA, DoMicroJump, DoMicroJump_IfCompare_AluA, HALT,
       Jump_Break, JumpDest_PlusOne, JumpDest_UseReg, JumpDest_UseRom, LoadInsn, LoadInsn_Direct,
       LoadInsn_IfJump, MicroJump_Break, mini_bit_extender_9_p1, mini_bit_extender_10_p1,
       mini_bit_selector_6_p11, mini_bit_selector_6_p13, MovByte_Write, MovRam_Addr_UsePayload,
       MovRam_Addr_UseReg, MovRam_WriteFromRam, MovRam_WriteToRam, MovRegisters_A, MovRegisters_B,
       MovRom_Write, MovTiny_Write, multiplexer_2_out, multiplexer_3_out, not_1_out, not_2_out, not_3_out,
       not_4_out, not_5_out, not_6_out, not_7_out, not_8_out, or_1_out, or_2_out, or_3_out, or_4_out,
       or_7_out, or_8_out, or_9_out, ProgramCounter_Advance, pull_resistor_1_node, pull_resistor_7_node,
       pull_resistor_8_node, pull_resistor_10_node, s_r_ff_1_qn, SerialWrite_Const, SerialWrite_t,
       ShouldMicroJump, ShouldPCJump, splitter_11_p1;
  wire [1:0] AluA_LeftConst_PayloadField, AluA_LeftReg_PayloadField, AluA_Op_PayloadField,
       AluA_OutReg_PayloadField, AluA_RightConst_PayloadField, AluA_RightReg_PayloadField,
       JumpCompare_AluAOp_Field, JumpDest_Reg_PayloadField, MovRam_AddrReg_PayloadField,
       MovRam_DataReg_PayloadField, MovRom_Reg_PayloadField, ProgramCounter_Advance_By,
       SerialWrite_Const_Field, SerialWrite_Reg_PayloadField;
  wire [2:0] counter_3_q, JumpCompare_AluAOp, LoadInsn_Source, MicroJumpCompare_AluAOp, Prefetch_Source,
       pull_resistor_13_node;
  wire [3:0] Payload_Override_Fields;
  wire [4:0] AluA_LeftConst, AluA_LeftReg, AluA_Op, AluA_OutReg, AluA_RightConst, AluA_RightReg,
       DivMod_DivDest, DivMod_Factor_Reg, DivMod_ModDest, DivMod_Src_Reg, JumpDest_Reg, MicroJump_Dest,
       MovRam_AddrReg, MovRam_DataReg, MovReg_DstA, MovReg_DstB, MovReg_SrcA, MovReg_SrcB, MovRom_Reg,
       MovTinyA_Reg, MovTinyB_Reg, multiplexer_18_out, SerialWrite_Reg, splitter_29_p2;
  wire [7:0] controlled_buffer_1_out, counter_2_q, DivMod_SerialWriteASCII_AssembledDigit, ram_2_dout;
  wire [14:0] RamAddr;
  wire [15:0] mini_bit_selector_1_p2, PC, PC_Next, Prefetch_RomAddr;
  wire [19:0] and_8_out, InsnPayload, Payload_Override, splitter_12_p1;
  wire [31:0] adder_2_out, adder_4_out, AluA_LeftReg_Value, AluA_LeftValue, AluA_Result, AluA_RightReg_Value,
       AluA_RightValue, controlled_buffer_3_out, controlled_buffer_5_out, controlled_buffer_6_out,
       DivMod_Factor, DivMod_Result_Div, DivMod_Result_Mod, DivMod_Src, IR_q, JumpDest, LoadInsn_Value,
       mini_bit_selector_6_p21, MovByte_Value, MovTinyA_Value, MovTinyB_Value, multiplexer_5_out,
       Prefetch_RomValue, pull_resistor_2_node, pull_resistor_3_node, pull_resistor_6_node, RamToRegValue,
       RegToRamValue, RomValue;

  // Mini_Bit_Selector #(.in_width(32), .out_width(16)) mini_bit_selector_1: pin names not known; wires that end beside it: JumpDest, mini_bit_selector_1_p2
  Pull_Resistor #(.pull(1)) pull_resistor_1 (.node(pull_resistor_1_node));
  Multiplexer #(.select(3), .width(16), .enable("false")) multiplexer_1 (
    .in0(PC), .in1(mini_bit_selector_1_p2), .in2(PC_Next), .out(Prefetch_RomAddr), .sel(Prefetch_Source));  // open: in3, in4, in5, in6, in7
  Adder #(.width(16)) adder_1 (.a(PC), .out(PC_Next), .cin(pull_resistor_1_node));  // open: b, cout
  Pull_Resistor pull_resistor_2 (.node(pull_resistor_2_node));
  ROM #(.addrWidth(16), .dataWidth(32), .sourcepath("asm/out.hex")) rom_1 (
    .addr(Prefetch_RomAddr), .data(Prefetch_RomValue));
  Comparator #(.width(32), .mode("unsigned")) comparator_1 (
    .a(AluA_Result), .b(pull_resistor_2_node), .gt(comparator_1_gt), .eq(comparator_1_eq),
    .lt(comparator_1_lt));
  Pull_Resistor pull_resistor_3 (.node(pull_resistor_3_node));
  not not_1 (not_1_out, comparator_1_gt);
  not not_2 (not_2_out, comparator_1_lt);
  Multiplexer #(.select(3), .enable("false")) multiplexer_2 (
    .in0(comparator_1_gt), .in1(not_1_out), .in2(comparator_1_eq), .in3(not_2_out), .in4(comparator_1_lt),
    .in5(not_3_out), .out(multiplexer_2_out), .sel(MicroJumpCompare_AluAOp));  // open: in6, in7
  not not_3 (not_3_out, comparator_1_eq);
  Comparator #(.width(32), .mode("unsigned")) comparator_2 (
    .a(AluA_Result), .b(pull_resistor_3_node), .gt(comparator_2_gt), .eq(comparator_2_eq),
    .lt(comparator_2_lt));
  and and_1 (and_1_out, multiplexer_2_out, DoMicroJump_IfCompare_AluA);
  not not_4 (not_4_out, comparator_2_gt);
  not not_5 (not_5_out, comparator_2_lt);
  Multiplexer #(.select(3), .enable("false")) multiplexer_3 (
    .in0(comparator_2_gt), .in1(not_4_out), .in2(comparator_2_eq), .in3(not_5_out), .in4(comparator_2_lt),
    .in5(not_6_out), .out(multiplexer_3_out), .sel(JumpCompare_AluAOp));  // open: in6, in7
  not not_6 (not_6_out, comparator_2_eq);
  // Splitter #(.appear("center"), .spacing("double")) splitter_1: pin names not known; wires that end beside it: ProgramCounter_Advance_By
  Pull_Resistor pull_resistor_4 (.node(MicroJump_Break));
  and and_2 (ShouldMicroJump, ~MicroJump_Break, or_1_out);  // AND_Gate
  or or_1 (or_1_out, and_1_out, DoMicroJump, LoadInsn);
  S_R_Flip_Flop s_r_ff_1 (.S(HALT), .Qn(s_r_ff_1_qn));  // open: R, clk, Q, reset, preset
  and and_3 (and_3_out, JumpDest_UseRom, ~ShouldPCJump);  // AND_Gate
  and and_4 (and_4_out, multiplexer_3_out, DoJump_IfCompare_AluA);
  Pull_Resistor pull_resistor_5 (.node(Jump_Break));
  // OR_Gate or_2 has open pins: out=or_2_out
  and and_5 (CLK_t, CLK, s_r_ff_1_qn);
  Adder #(.width(32)) adder_2 (
    .a(JumpDest), .b(pull_resistor_6_node), .out(adder_2_out), .cin(JumpDest_PlusOne));  // open: cout
  Pull_Resistor pull_resistor_6 (.node(pull_resistor_6_node));
  and and_6 (ShouldPCJump, ~Jump_Break, or_3_out);  // AND_Gate
  or or_3 (or_3_out, and_4_out, DoJump, or_2_out);
  ROM #(.addrWidth(16), .dataWidth(32), .sourcepath("asm/out.hex")) PROG (.addr(PC), .data(RomValue));
  Counter #(.width(16), .max('hffff)) counter_1 (
    .load(ShouldPCJump), .up(pull_resistor_7_node), .count(or_4_out), .clk(CLK_t), .Q(PC));  // open: clr, D, carry
  Pull_Resistor #(.pull(1)) pull_resistor_7 (.node(pull_resistor_7_node));
  or or_4 (or_4_out, ProgramCounter_Advance, and_3_out);
  // Mini_Bit_Selector #(.in_width(32), .out_width(16)) mini_bit_selector_2: pin names not known; wires that end beside it: adder_2_out
  Counter counter_2 (
    .load(ShouldMicroJump), .up(pull_resistor_8_node), .count(not_7_out), .clk(CLK_t), .Q(counter_2_q));  // open: clr, D, carry
  Pull_Resistor #(.pull(1)) pull_resistor_8 (.node(pull_resistor_8_node));
  not not_7 (not_7_out, ShouldMicroJump);
  // Mini_Bit_Extender #(.in_width(5), .out_width(8), .\type ("zero")) mini_bit_extender_1: pin names not known; wires that end beside it: MicroJump_Dest
  Register #(.width(32)) IR (.D(LoadInsn_Value), .en(LoadInsn), .clk(CLK_t), .Q(IR_q));  // open: clr
  Button button_1 (.out(button_1_out));
  not not_8 (not_8_out, button_1_out);
  assign controlled_buffer_1_out = not_8_out ? counter_2_q : 8'bz;  // Controlled_Buffer controlled_buffer_1
  assign JumpDest = JumpDest_UseRom ? RomValue : 32'bz;  // Controlled_Buffer controlled_buffer_2
  RAM #(.addrWidth(15), .dataWidth(32), .databus("bibus")) ram_1 (
    .addr(RamAddr), .we(MovRam_WriteToRam), .oe(MovRam_WriteFromRam), .clk(CLK_t), .din(RegToRamValue),
    .dout(RamToRegValue));
  and and_7 (and_7_out, LoadInsn_IfJump, ShouldPCJump);
  // Big_ROM #(.addressWidth(20), .valueWidth(128), .sourcepath("run/out/v2/microcode.hex")) big_rom_1: pin names not known; wires that end beside it: big_rom_1_p1, big_rom_1_p2, big_rom_1_p3
  // Splitter #(.fanout(32), .incoming(32), .appear("right"), .spacing("double")) splitter_2: pin names not known; wires that end beside it: big_rom_1_p1, HALT, LoadInsn_Direct
  // Splitter #(.appear("center"), .spacing("double")) splitter_3: pin names not known; wires that end beside it: ProgramCounter_Advance, MovRom_Write, MovRom_Reg_PayloadField
  // Splitter #(.appear("center"), .spacing("double")) splitter_4: pin names not known; wires that end beside it: AluA_LeftReg_PayloadField
  // Splitter #(.appear("center"), .spacing("double")) splitter_5: pin names not known; wires that end beside it: AluA_RightReg_PayloadField
  // Splitter #(.appear("center"), .spacing("double")) splitter_6: pin names not known; wires that end beside it: AluA_OutReg_PayloadField
  // Splitter #(.appear("center"), .spacing("double")) splitter_7: pin names not known; wires that end beside it: AluA_EnableSigned, AluA_WriteOutput, DoJump, AluA_Op_PayloadField
  // Splitter #(.appear("center"), .spacing("double")) splitter_8: pin names not known; wires that end beside it: JumpDest_UseRom, JumpDest_UseReg, MovByte_Write, MovTiny_Write, JumpDest_Reg_PayloadField
  // Splitter #(.appear("center"), .spacing("double")) splitter_9: pin names not known; wires that end beside it: DoJump_IfCompare_AluA, MovRam_WriteToRam, MovRam_WriteFromRam, JumpCompare_AluAOp_Field
  // Splitter #(.appear("center"), .spacing("double")) splitter_10: pin names not known; wires that end beside it: MovRam_Addr_UsePayload, MovRam_Addr_UseReg, MovRam_DataReg_PayloadField
  or or_5 (LoadInsn, LoadInsn_Direct, and_7_out);
  Pull_Resistor pull_resistor_9 (.node(LoadInsn_Source));
  Multiplexer #(.select(3), .width(32), .enable("false")) multiplexer_4 (
    .in0(RomValue), .in1(Prefetch_RomValue), .out(LoadInsn_Value), .sel(LoadInsn_Source));  // open: in2, in3, in4, in5, in6, in7
  // Splitter #(.fanout(4), .incoming(4), .appear("center"), .spacing("double")) splitter_11: pin names not known; wires that end beside it: splitter_11_p1, Payload_Override_Fields
  // Mini_Bit_Extender #(.in_width(1), .out_width(5)) mini_bit_extender_2: pin names not known
  // NOT_Gate not_9 is placed but not wired
  // NOT_Gate not_10 is placed but not wired
  // Mini_Bit_Extender #(.in_width(1), .out_width(5)) mini_bit_extender_3: pin names not known
  // Mini_Bit_Extender #(.in_width(1), .out_width(5)) mini_bit_extender_4: pin names not known
  // NOT_Gate not_11 is placed but not wired
  // Splitter #(.fanout(4), .incoming(20), .appear("center"), .spacing("double"), .bit1(0), .bit2(0), .bit3(0), .bit4(0), .bit5(1), .bit6(1), .bit7(1), .bit8(1), .bit9(1), .bit10(2), .bit11(2), .bit12(2), .bit13(2), .bit14(2), .bit15(3), .bit16(3), .bit17(3), .bit18(3), .bit19(3)) splitter_12: pin names not known; wires that end beside it: splitter_12_p1
  // Mini_Bit_Extender #(.in_width(1), .out_width(5)) mini_bit_extender_5: pin names not known
  // NOT_Gate not_12 is placed but not wired
  // Splitter #(.fanout(32), .incoming(32), .appear("right"), .spacing("double")) splitter_13: pin names not known; wires that end beside it: big_rom_1_p2
  assign and_8_out = splitter_12_p1 & IR_q[19:0];  // AND_Gate and_8, 20 bits wide
  // Splitter #(.appear("center"), .spacing("double")) splitter_14: pin names not known; wires that end beside it: MovRam_AddrReg_PayloadField
  // Splitter #(.appear("center"), .spacing("double")) splitter_15: pin names not known; wires that end beside it: AluA_LeftConst_PayloadField
  // Splitter #(.appear("center"), .spacing("double")) splitter_16: pin names not known; wires that end beside it: AluA_Left_UseConst, AluA_Right_UseConst, MovRegisters_A, AluA_RightConst_PayloadField
  // Splitter #(.fanout(3), .incoming(3), .appear("center"), .spacing("double")) splitter_17: pin names not known; wires that end beside it: MovRegisters_B, Prefetch_Source
  // Splitter #(.appear("center"), .spacing("double")) splitter_18: pin names not known; wires that end beside it: JumpDest_PlusOne, ProgramCounter_Advance_By
  // Splitter #(.fanout(3), .incoming(3), .appear("center"), .spacing("double")) splitter_19: pin names not known; wires that end beside it: LoadInsn_IfJump, LoadInsn_Source
  // Splitter #(.fanout(5), .incoming(5), .appear("center"), .spacing("double")) splitter_20: pin names not known; wires that end beside it: DoMicroJump, MicroJump_Dest
  // Splitter #(.fanout(3), .incoming(3), .appear("center"), .spacing("double")) splitter_21: pin names not known; wires that end beside it: DoMicroJump_IfCompare_AluA, MicroJumpCompare_AluAOp
  // Splitter #(.appear("center"), .spacing("double")) splitter_22: pin names not known; wires that end beside it: SerialWrite_Reg_PayloadField
  assign InsnPayload = Payload_Override | and_8_out;  // OR_Gate or_6, 20 bits wide
  // Splitter #(.appear("center"), .spacing("double")) splitter_23: pin names not known; wires that end beside it: ProgramCounter_Advance_By
  or or_7 (or_7_out, AluA_WriteOutput, DoJump_IfCompare_AluA);
  // OR_Gate or_8 has open pins: out=or_8_out
  Pull_Resistor #(.pull(1)) pull_resistor_10 (.node(pull_resistor_10_node));
  // Mini_Bit_Extender #(.in_width(2), .\type ("zero")) mini_bit_extender_6: pin names not known
  Adder #(.width(16)) adder_3 (.b(PC), .cin(pull_resistor_10_node));  // open: a, out, cout
  // Mini_Bit_Extender #(.in_width(16), .out_width(32)) mini_bit_extender_7: pin names not known
  Pull_Resistor pull_resistor_11 (.node(AluA_LeftValue));
  // ALU #(.width(32)) alu_1: pin names not known; wires that end beside it: AluA_EnableSigned, AluA_Op, AluA_LeftValue, AluA_RightValue, AluA_Result
  // Probe on controlled_buffer_3_out
  // Probe on controlled_buffer_3_out
  assign controlled_buffer_3_out = or_7_out ? AluA_LeftValue : 32'bz;  // Controlled_Buffer controlled_buffer_3
  // Splitter #(.fanout(32), .incoming(32), .appear("right"), .spacing("double")) splitter_24: pin names not known; wires that end beside it: big_rom_1_p3, SerialWrite_t, DivMod_Write, DivMod_UseConst
  // Splitter #(.fanout(4), .incoming(4), .appear("center"), .spacing("double")) splitter_25: pin names not known; wires that end beside it: DivMod_SerialWriteASCII_Assembling, Payload_Override_Fields
  // Splitter #(.fanout(20), .incoming(20), .appear("center"), .spacing("double")) splitter_26: pin names not known; wires that end beside it: Payload_Override
  // Splitter #(.appear("center"), .spacing("double")) splitter_27: pin names not known; wires that end beside it: SerialWrite_Const, DivMod_SerialWriteASCII_Writing, SerialWrite_Const_Field
  Controlled_Buffer #(.width(32)) controlled_buffer_4 (.out(JumpDest), .en(or_8_out));  // open: in
  Pull_Resistor pull_resistor_12 (.node(AluA_RightValue));
  // Probe on controlled_buffer_5_out
  assign controlled_buffer_5_out = or_7_out ? AluA_RightValue : 32'bz;  // Controlled_Buffer controlled_buffer_5
  // Probe on controlled_buffer_5_out
  // Splitter #(.fanout(32), .incoming(32), .appear("right"), .spacing("double")) splitter_28: pin names not known; wires that end beside it: splitter_11_p1
  or or_9 (or_9_out, DivMod_SerialWriteASCII_Assembling, DivMod_SerialWriteASCII_Writing);
  // Probe on controlled_buffer_6_out
  assign controlled_buffer_6_out = or_7_out ? AluA_Result : 32'bz;  // Controlled_Buffer controlled_buffer_6
  // Probe on controlled_buffer_6_out
  Counter #(.width(3), .max('h7)) counter_3 (
    .load(counter_3_carry), .up(DivMod_SerialWriteASCII_Assembling), .count(or_9_out), .clk(CLK_t),
    .D(pull_resistor_13_node), .carry(counter_3_carry), .Q(counter_3_q));  // open: clr
  Pull_Resistor pull_resistor_13 (.node(pull_resistor_13_node));
  // Splitter #(.fanout(4), .incoming(20), .appear("center"), .spacing("double"), .bit1(0), .bit2(0), .bit3(0), .bit4(0), .bit5(1), .bit6(1), .bit7(1), .bit8(1), .bit9(1), .bit10(2), .bit11(2), .bit12(2), .bit13(2), .bit14(2), .bit15(3), .bit16(3), .bit17(3), .bit18(3), .bit19(3)) splitter_29: pin names not known; wires that end beside it: InsnPayload, splitter_29_p2, DivMod_ModDest, DivMod_DivDest, DivMod_Src_Reg
  Comparator #(.width(32), .mode("unsigned")) comparator_3 (
    .a(DivMod_Result_Mod), .b(32'h9), .gt(comparator_3_gt));  // open: eq, lt
  assign MicroJump_Break = DivMod_SerialWriteASCII_Writing ? counter_3_carry : 1'bz;  // Controlled_Buffer controlled_buffer_7
  RAM #(.addrWidth(3), .databus("bibus")) ram_2 (
    .addr(counter_3_q), .we(DivMod_SerialWriteASCII_Assembling), .oe(DivMod_SerialWriteASCII_Writing),
    .clk(CLK_t), .din(DivMod_SerialWriteASCII_AssembledDigit), .dout(ram_2_dout));
  // Splitter #(.fanout(4), .incoming(20), .appear("center"), .spacing("double"), .bit1(0), .bit2(0), .bit3(0), .bit4(0), .bit5(1), .bit6(1), .bit7(1), .bit8(1), .bit9(1), .bit10(2), .bit11(2), .bit12(2), .bit13(2), .bit14(2), .bit15(3), .bit16(3), .bit17(3), .bit18(3), .bit19(3)) splitter_30: pin names not known; wires that end beside it: InsnPayload, MovTinyB_Reg, MovTinyA_Reg
  // Mini_Bit_Selector #(.in_width(20), .out_width(15)) mini_bit_selector_3: pin names not known; wires that end beside it: InsnPayload
  // Splitter #(.fanout(4), .incoming(20), .appear("center"), .spacing("double"), .bit1(0), .bit2(0), .bit3(0), .bit4(0), .bit5(1), .bit6(1), .bit7(1), .bit8(1), .bit9(1), .bit10(2), .bit11(2), .bit12(2), .bit13(2), .bit14(2), .bit15(3), .bit16(3), .bit17(3), .bit18(3), .bit19(3)) splitter_31: pin names not known; wires that end beside it: InsnPayload, MovReg_DstB, MovReg_SrcB, MovReg_DstA, MovReg_SrcA
  Demultiplexer #(.width(5), .disabled("Z"), .enable("false")) demultiplexer_1 (
    .out0(DivMod_Factor_Reg), .in(splitter_29_p2), .sel(DivMod_UseConst));  // open: out1
  Multiplexer #(.width(32), .enable("false")) multiplexer_5 (
    .in0(32'h30), .in1(32'h37), .out(multiplexer_5_out), .sel(comparator_3_gt));
  Adder #(.width(32)) adder_4 (.a(multiplexer_5_out), .b(DivMod_Result_Mod), .out(adder_4_out));  // open: cin, cout
  Multiplexer #(.select(2), .width(5), .enable("false")) multiplexer_6 (
    .in0(InsnPayload[4:0]), .in1(InsnPayload[9:5]), .in2(InsnPayload[14:10]), .in3(InsnPayload[19:15]),
    .out(MovRom_Reg), .sel(MovRom_Reg_PayloadField));
  Multiplexer #(.select(2), .width(5), .enable("false")) multiplexer_7 (
    .in0(InsnPayload[4:0]), .in1(InsnPayload[9:5]), .in2(InsnPayload[14:10]), .in3(InsnPayload[19:15]),
    .out(AluA_LeftReg), .sel(AluA_LeftReg_PayloadField));
  Multiplexer #(.select(2), .width(5), .enable("false")) multiplexer_8 (
    .in0(InsnPayload[4:0]), .in1(InsnPayload[9:5]), .in2(InsnPayload[14:10]), .in3(InsnPayload[19:15]),
    .out(AluA_RightReg), .sel(AluA_RightReg_PayloadField));
  Multiplexer #(.select(2), .width(5), .enable("false")) multiplexer_9 (
    .in0(InsnPayload[4:0]), .in1(InsnPayload[9:5]), .in2(InsnPayload[14:10]), .in3(InsnPayload[19:15]),
    .out(AluA_OutReg), .sel(AluA_OutReg_PayloadField));
  Multiplexer #(.select(2), .width(5), .enable("false")) multiplexer_10 (
    .in0(InsnPayload[4:0]), .in1(InsnPayload[9:5]), .in2(InsnPayload[14:10]), .in3(InsnPayload[19:15]),
    .out(AluA_Op), .sel(AluA_Op_PayloadField));
  Multiplexer #(.select(2), .width(5), .enable("false")) multiplexer_11 (
    .in0(InsnPayload[4:0]), .in1(InsnPayload[9:5]), .in2(InsnPayload[14:10]), .in3(InsnPayload[19:15]),
    .out(JumpDest_Reg), .sel(JumpDest_Reg_PayloadField));
  Multiplexer #(.select(2), .width(5), .enable("false")) multiplexer_12 (
    .in0(InsnPayload[4:0]), .in1(InsnPayload[9:5]), .in2(InsnPayload[14:10]), .in3(InsnPayload[19:15]),
    .out(AluA_LeftConst), .sel(AluA_LeftConst_PayloadField));
  Multiplexer #(.select(2), .width(5), .enable("false")) multiplexer_13 (
    .in0(InsnPayload[4:0]), .in1(InsnPayload[9:5]), .in2(InsnPayload[14:10]), .in3(InsnPayload[19:15]),
    .out(AluA_RightConst), .sel(AluA_RightConst_PayloadField));
  // Mini_Bit_Extender #(.out_width(32)) mini_bit_extender_8: pin names not known; wires that end beside it: InsnPayload[7:0], MovByte_Value
  // Mini_Bit_Extender #(.in_width(5), .out_width(32)) mini_bit_extender_9: pin names not known; wires that end beside it: mini_bit_extender_9_p1, mini_bit_extender_9_p1, MovTinyB_Value
  // Mini_Bit_Extender #(.in_width(5), .out_width(32)) mini_bit_extender_10: pin names not known; wires that end beside it: mini_bit_extender_10_p1, mini_bit_extender_10_p1, MovTinyA_Value
  Controlled_Buffer #(.width(15)) controlled_buffer_8 (.out(RamAddr), .en(MovRam_Addr_UsePayload));  // open: in
  Multiplexer #(.select(2), .width(5), .enable("false")) multiplexer_14 (
    .in0(InsnPayload[4:0]), .in1(InsnPayload[9:5]), .in2(InsnPayload[14:10]), .in3(InsnPayload[19:15]),
    .out(MovRam_AddrReg), .sel(MovRam_AddrReg_PayloadField));
  Multiplexer #(.select(2), .width(5), .enable("false")) multiplexer_15 (
    .in0(InsnPayload[4:0]), .in1(InsnPayload[9:5]), .in2(InsnPayload[14:10]), .in3(InsnPayload[19:15]),
    .out(MovRam_DataReg), .sel(MovRam_DataReg_PayloadField));
  Multiplexer #(.select(2), .width(5), .enable("false")) multiplexer_16 (
    .in0(InsnPayload[4:0]), .in1(InsnPayload[9:5]), .in2(InsnPayload[14:10]), .in3(InsnPayload[19:15]),
    .sel(JumpCompare_AluAOp_Field));  // open: out
  // Mini_Bit_Selector #(.in_width(5), .out_width(3)) mini_bit_selector_4: pin names not known; wires that end beside it: JumpCompare_AluAOp
  Multiplexer #(.select(2), .width(5), .enable("false")) multiplexer_17 (
    .in0(InsnPayload[4:0]), .in1(InsnPayload[9:5]), .in2(InsnPayload[14:10]), .in3(InsnPayload[19:15]),
    .out(SerialWrite_Reg), .sel(SerialWrite_Reg_PayloadField));
  Multiplexer #(.select(2), .width(5), .enable("false")) multiplexer_18 (
    .in0(InsnPayload[4:0]), .in1(InsnPayload[9:5]), .in2(InsnPayload[14:10]), .in3(InsnPayload[19:15]),
    .out(multiplexer_18_out), .sel(SerialWrite_Const_Field));
  // Mini_Bit_Extender #(.in_width(5), .out_width(32), .\type ("zero")) mini_bit_extender_11: pin names not known; wires that end beside it: multiplexer_18_out
  Controlled_Buffer #(.width(32)) controlled_buffer_9 (.out(SerialOut), .en(SerialWrite_Const));  // open: in
  Controlled_Buffer #(.width(32)) controlled_buffer_10 (.out(DivMod_Factor), .en(DivMod_UseConst));  // open: in
  // Mini_Bit_Extender #(.in_width(5), .out_width(32), .\type ("zero")) mini_bit_extender_12: pin names not known
  or or_10 (SerialWrite, DivMod_SerialWriteASCII_Writing, SerialWrite_Const, SerialWrite_t);
  // Mini_Bit_Selector #(.in_width(32)) mini_bit_selector_5: pin names not known; wires that end beside it: adder_4_out, DivMod_SerialWriteASCII_AssembledDigit
  // Mini_Bit_Extender #(.out_width(32), .\type ("zero")) mini_bit_extender_13: pin names not known; wires that end beside it: ram_2_dout
  Controlled_Buffer #(.width(32)) controlled_buffer_11 (
    .out(SerialOut), .en(DivMod_SerialWriteASCII_Writing));  // open: in
  Divider #(.width(32)) divider_1 (
    .a(DivMod_Src), .b(DivMod_Factor), .out(DivMod_Result_Div), .rem(DivMod_Result_Mod));  // open: upper
  Multiplexer #(.width(32), .enable("false")) multiplexer_19 (
    .in0(AluA_LeftReg_Value), .out(AluA_LeftValue), .sel(AluA_Left_UseConst));  // open: in1
  // Mini_Bit_Extender #(.in_width(5), .out_width(32)) mini_bit_extender_14: pin names not known; wires that end beside it: AluA_LeftConst
  Multiplexer #(.width(32), .enable("false")) multiplexer_20 (
    .in0(AluA_RightReg_Value), .out(AluA_RightValue), .sel(AluA_Right_UseConst));  // open: in1
  // Mini_Bit_Extender #(.in_width(5), .out_width(32)) mini_bit_extender_15: pin names not known; wires that end beside it: AluA_RightConst
  // Register_Bank #(.width(32), .registerCount(32), .portCount(32)) register_bank_1: pin names not known; wires that end beside it: JumpDest_Reg, AluA_OutReg, AluA_RightReg, AluA_LeftReg, MovRom_Reg, CLK_t, MovByte_Value, AluA_WriteOutput, AluA_Result, MovRom_Write, RomValue, out_4, AluA_RightReg_Value, AluA_LeftReg_Value
  // NOT_Gate not_13 has open pins: in=DivMod_UseConst, out=open
  assign SerialOut = SerialWrite_t ? mini_bit_selector_6_p21 : 32'bz;  // Controlled_Buffer controlled_buffer_12
  // Mini_Bit_Selector #(.in_width(32), .out_width(15)) mini_bit_selector_6: pin names not known; wires that end beside it: MovReg_DstB, MovReg_SrcB, MovReg_DstA, MovReg_SrcA, MovRam_AddrReg, MovRam_DataReg, MovTinyB_Reg, MovTinyA_Reg, InsnPayload[19:15], MovRegisters_B, mini_bit_selector_6_p11, MovRegisters_A, mini_bit_selector_6_p13, MovRam_WriteFromRam, RamToRegValue, MovTiny_Write, MovTinyB_Value, MovTiny_Write, MovTinyA_Value, RegToRamValue, mini_bit_selector_6_p21, mini_bit_selector_6_p11, mini_bit_selector_6_p13, MovRam_Addr_UseReg, JumpDest_UseReg, JumpDest, RamAddr

  // Other names for the same wires on the sheet: DoSerialWrite = SerialWrite; MovByte_Reg[4:0] = InsnPayload[19:15]

  // Notes on the sheet:
  //   SerialWrite: pull=down
  //   contents of rom_1 (hex, n*v repeats v):
  //   30003a 1600010 1750000 b00020 700000 1
  //   contents of PROG (hex, n*v repeats v):
  //   30003a 1600010 1750000 b00020 700000 1
  //   ±
  //   +
  //   =
endmodule

module viewer (
);

  wire buffer_1_out, CLK, clock_1_out, main_1_serialwrite;
  wire [6:0] mini_bit_selector_1_p2;
  wire [31:0] main_1_serialout;

  Clock clock_1 (.out(clock_1_out));
  xor xor_1 (CLK, clock_1_out, buffer_1_out);
  buf buffer_1 (buffer_1_out, clock_1_out);
  main main_1 (.CLK(CLK), .SerialWrite(main_1_serialwrite), .SerialOut(main_1_serialout));  // open: out_4
  // Probe on main_1_serialout
  // Mini_Bit_Selector #(.in_width(32), .out_width(7)) mini_bit_selector_1: pin names not known; wires that end beside it: main_1_serialout, mini_bit_selector_1_p2
  TTY tty_1 (.data(mini_bit_selector_1_p2), .clk(CLK), .we(main_1_serialwrite));  // open: clr
endmodule
